# Fritzing sketch diagrama_actuador_led (saved by Fritzing 0.9.6b)
breadboards: 1

parts:
  U1 = NodeMCU V3.0
  LED1 = LED - 5mm [color="Red (633nm)" current=0.030 package="5 mm [THT]"]
  LED2 = LED - 5mm [color="Red (633nm)" current=0.030 package="5 mm [THT]"]
  LED3 = LED - 5mm [color="Red (633nm)" current=0.030 package="5 mm [THT]"]

nets:
  N1: U1.D1, LED3.anode
  N2: U1.D2, LED2.anode
  N3: U1.D3, LED1.anode
  N4: U1.GND, LED1.cathode, LED2.cathode, LED3.cathode

custom parts:
  NodeMCU V3.0: ESP8266 based NodeMCU
